// Logisim project 24h_clock.circ as structural Verilog: 1 circuit, main circuit main
module main (
);

  wire and_1_out, and_2_out, and_3_out, and_4_out, and_5_out, and_6_out, and_7_out, and_8_out, clock_1_out,
       j_k_ff_1_q, j_k_ff_2_q, j_k_ff_3_q, j_k_ff_4_q, j_k_ff_5_q, j_k_ff_6_q, j_k_ff_6_qn, j_k_ff_7_q,
       j_k_ff_7_qn, j_k_ff_8_q, not_1_out, not_2_out, not_3_out, not_4_out, or_1_out, or_2_out, or_3_out,
       or_4_out, or_5_out, or_6_out, or_7_out, or_8_out, P_R_out, P_RSa_out, PaQa_out, PaQaR_out, QaSa_out,
       QRa_out, QRaS_out, QS_out, QSa_out, RaSa_out, RS_out, RSa_out, undriven, undriven_2, undriven_3,
       undriven_4, undriven_5, undriven_6, undriven_7;

  _7_Segment_Display #(.decimalPoint("false")) u_7_segment_display_1 ();  // open: g, f, a, b, e, d, c
  _7_Segment_Display u_7_segment_display_2 (.dp(1'b1));  // open: g, f, a, b, e, d, c
  _7_Segment_Display #(.decimalPoint("false")) u_7_segment_display_3 ();  // open: g, f, a, b, e, d, c
  _7_Segment_Display u_7_segment_display_4 (.dp(1'b1));  // open: g, f, a, b, e, d, c
  _7_Segment_Display #(.decimalPoint("false")) u_7_segment_display_5 (
    .g(undriven_2), .f(undriven), .a(undriven_5), .b(undriven_7), .e(undriven_3), .d(undriven_4),
    .c(undriven_6));
  _7_Segment_Display #(.decimalPoint("false")) u_7_segment_display_6 (
    .g(or_7_out), .f(or_8_out), .a(or_2_out), .b(or_3_out), .e(or_4_out), .d(or_6_out), .c(or_1_out));
  J_K_Flip_Flop j_k_ff_1 (
    .J(and_5_out), .K(and_5_out), .clk(clock_1_out), .Q(j_k_ff_1_q), .reset(and_1_out));  // open: Qn, preset
  Clock clock_1 (.out(clock_1_out));
  not not_1 (not_1_out, j_k_ff_5_q);
  and and_1 (and_1_out, j_k_ff_2_q, j_k_ff_3_q);
  not not_2 (not_2_out, j_k_ff_6_q);
  and and_2 (and_2_out, and_5_out, j_k_ff_1_q);
  J_K_Flip_Flop j_k_ff_2 (
    .J(and_2_out), .K(and_2_out), .clk(clock_1_out), .Q(j_k_ff_2_q), .reset(and_1_out));  // open: Qn, preset
  not not_3 (not_3_out, j_k_ff_7_q);
  not not_4 (not_4_out, j_k_ff_8_q);
  and and_3 (and_3_out, and_2_out, j_k_ff_2_q);
  J_K_Flip_Flop j_k_ff_3 (
    .J(and_3_out), .K(and_3_out), .clk(clock_1_out), .Q(j_k_ff_3_q), .reset(and_1_out));  // open: Qn, preset
  or P_R (P_R_out, j_k_ff_8_q, j_k_ff_6_q);
  and QS (QS_out, j_k_ff_7_q, j_k_ff_5_q);
  and QaSa (QaSa_out, not_3_out, not_1_out);
  and PaQa (PaQa_out, not_4_out, not_3_out);
  and RaSa (RaSa_out, not_2_out, not_1_out);
  and RS (RS_out, j_k_ff_6_q, j_k_ff_5_q);
  or or_1 (or_1_out, j_k_ff_8_q, j_k_ff_7_q, not_2_out, j_k_ff_5_q);
  and RSa (RSa_out, j_k_ff_6_q, not_1_out);
  and QRa (QRa_out, j_k_ff_7_q, not_2_out);
  and QSa (QSa_out, j_k_ff_7_q, not_1_out);
  and and_4 (and_4_out, and_3_out, j_k_ff_3_q);
  J_K_Flip_Flop j_k_ff_4 (
    .J(and_4_out), .K(and_4_out), .clk(clock_1_out), .Q(j_k_ff_4_q), .reset(and_1_out));  // open: Qn, preset
  or or_2 (or_2_out, P_R_out, QS_out, QaSa_out);
  or or_3 (or_3_out, j_k_ff_8_q, PaQa_out, RaSa_out, RS_out);
  or or_4 (or_4_out, QaSa_out, RSa_out);
  or P_RSa (P_RSa_out, j_k_ff_8_q, RSa_out);
  and QRaS (QRaS_out, j_k_ff_5_q, QRa_out);
  and PaQaR (PaQaR_out, PaQa_out, j_k_ff_6_q);
  or or_5 (or_5_out, RaSa_out, j_k_ff_8_q);
  or or_6 (or_6_out, QaSa_out, P_RSa_out, QRaS_out, PaQaR_out);
  or or_7 (or_7_out, P_RSa_out, PaQaR_out, QRa_out);
  or or_8 (or_8_out, or_5_out, QRa_out, QSa_out);
  and and_5 (and_5_out, j_k_ff_8_q, j_k_ff_7_qn, j_k_ff_6_qn, j_k_ff_5_q);
  J_K_Flip_Flop j_k_ff_5 (
    .J(1'b1), .K(1'b1), .clk(clock_1_out), .Q(j_k_ff_5_q), .reset(and_6_out));  // open: Qn, preset
  and and_6 (and_6_out, j_k_ff_6_q, j_k_ff_8_q);
  J_K_Flip_Flop j_k_ff_6 (
    .J(j_k_ff_5_q), .K(j_k_ff_5_q), .clk(clock_1_out), .Q(j_k_ff_6_q), .Qn(j_k_ff_6_qn), .reset(and_6_out));  // open: preset
  and and_7 (and_7_out, j_k_ff_5_q, j_k_ff_6_q);
  J_K_Flip_Flop j_k_ff_7 (
    .J(and_7_out), .K(and_7_out), .clk(clock_1_out), .Q(j_k_ff_7_q), .Qn(j_k_ff_7_qn), .reset(and_6_out));  // open: preset
  and and_8 (and_8_out, and_7_out, j_k_ff_7_q);
  J_K_Flip_Flop j_k_ff_8 (
    .J(and_8_out), .K(and_8_out), .clk(clock_1_out), .Q(j_k_ff_8_q), .reset(and_6_out));  // open: Qn, preset

  // Notes on the sheet:
  //   S
  //   Q
  //   R
  //   P
endmodule
